# Fritzing sketch KilnControllerRPi (saved by Fritzing 0.9.3b)

parts:
  J2 = Screw terminal - 2 pins [package=THT]
  J3 = female pin header, 2 pins [form="♀ (female)"]
  R2 = Resistor [tolerance=±5% resistance=32.5 power=1.8kW package=THT]
  R1 = Resistor [tolerance=±5% resistance=32.5 power=1.8kW package=THT]
  Raspberry_Pi_1 = Raspberry Pi 3 [part_number=RPI-3-V1.2]
  J1 = screw terminal, 3 pins
  Part2 = Adafruit Thermocouple Amplifier MAX31855 [part_number="Adafruit #269"]
  S1 = Pushbutton [package=THT]
  U5 = RELAY-SOLIDSTATE [package=relay-s108t02]
  R3 = Resistor [tolerance=±5% resistance=10k power=0.25W package="1206 [SMD]"]

nets:
  AC neutral: J2.pin1, R2.Pin_1, R1.Pin_1, J1.pin2
  AC active: J2.pin2, J1.pin1, U5.T2
  +5v: J3.pin1, Raspberry_Pi_1.5V, R3.Pin_0
  gnd: J3.pin2, Raspberry_Pi_1.GND, Part2.GND, S1.leg0, U5.-
  N1: R2.Pin_0, R1.Pin_0, U5.T1
  +3v3: Raspberry_Pi_1.3v3, Raspberry_Pi_1.3V3, Part2.+3V3
  N2: Raspberry_Pi_1.GIPO17, Part2.DO
  N3: Raspberry_Pi_1.GIPO27, Part2.CS
  N4: Raspberry_Pi_1.GIPO22, Part2.CLK
  N5: Raspberry_Pi_1.GIPO12, S1.leg1, R3.Pin_1
  N6: Raspberry_Pi_1.GIPO23, U5.+
  AC ground: J1.pin3
  k type thermocouple: Part2.THERMO-, Part2.THERMO+

notes:
  Heating Elements
  DC Supply
  Door Safety
  Temperature Sensor
  15A AC Input
  Raspberry Pi 3
  240V Input
  5V Supply
  Elements
  Door Switch

custom parts:
  Adafruit Thermocouple Amplifier MAX31855: Thermocouples are very sensitive, requiring a good amplifier with a cold-compensation reference. The MAX31855K does everything for you, and can be easily interfaced with any microcontroller, even one without an analog input. This breakout board has the chip itself, a 3.3V regulator with 10uF bypass capacitors and level shifting circuitry, all assembled and tested. Comes with a 2 pin terminal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
